// Logisim project s-mips.circ as structural Verilog
module S_MIPS_Board (
  input  in_1,
  input  DESHABILITAR_DISPATCHER,
  output halt
);

  wire button_1_out, CLK, CS, d_ff_1_q, LCLR, LoadRAM, LoadRAMOn, LW, R_R_W, R_W, ram_dispatcher_1_finished,
       RCS, Reset_out, RST, TTY_EN;
  wire [2:0] KDB;
  wire [3:0] LMask, Mask, ram_1_read_time, ram_1_write_time, RMask;
  wire [6:0] KDB_DATA, TTY_DATA;
  wire [15:0] Addr, LAddr, RAddr;
  wire [31:0] I0, I1, I2, I3, LData, ram_1_data_out_0, ram_1_data_out_1, ram_1_data_out_2, ram_1_data_out_3,
       RI0, RI1, RI2, RI3;

  TTY #(.rows(25), .cols(80)) tty_1 (.data(TTY_DATA), .clk(CLK), .we(TTY_EN), .clr(RST));
  not not_1 (LoadRAMOn, ram_dispatcher_1_finished);
  RAM_Dispatcher ram_dispatcher_1 (
    .WriteTime(ram_1_write_time), .Clock(CLK), .Data(LData), .Address(LAddr), .Mask(LMask),
    .Finished(ram_dispatcher_1_finished), .Write(LW), .CLR(LCLR));
  Keyboard #(.buflen(64)) keyboard_1 (.clk(CLK), .re(KDB[0]), .avail(KDB[2]), .data(KDB_DATA));  // open: clr
  RAM ram_1 (
    .Address(RAddr), .Data_Out_0(ram_1_data_out_0), .Data_Out_1(ram_1_data_out_1),
    .Data_Out_2(ram_1_data_out_2), .Data_Out_3(ram_1_data_out_3), .Data_In_0(RI0), .Data_In_1(RI1),
    .Data_In_2(RI2), .Data_In_3(RI3), .Mask(RMask), .nRead_Write(R_R_W), .Chip_Select(RCS),
    .Read_Time(ram_1_read_time), .Reset(button_1_out), .Write_Time(ram_1_write_time));
  Button button_1 (.out(button_1_out));
  D_Flip_Flop d_ff_1 (.clk(CLK), .D(1'b1), .Q(d_ff_1_q), .reset(Reset_out));  // open: Qn, preset, en
  Button Reset (.out(Reset_out));
  // Probe on ram_1_data_out_0
  S_MIPS s_mips_1 (
    .Kbd_Enable(KDB[0]), .Address(Addr), .Kbd_Clear(KDB[1]), .Kbd_Available(KDB[2]), .RAM_In_0(I0),
    .Kbd_ASCII_Data(KDB_DATA), .RAM_In_1(I1), .TTY_Enable(TTY_EN), .RAM_In_2(I2), .RAM_In_3(I3),
    .TTY_ASCII_Data(TTY_DATA), .Reset(RST), .RAM_Out_0(ram_1_data_out_0), .Clock(CLK),
    .RAM_Out_1(ram_1_data_out_1), .Stop(halt), .RAM_Out_2(ram_1_data_out_2), .RAM_Out_3(ram_1_data_out_3),
    .Mask(Mask), .Read_Time(ram_1_read_time), .Write_Time(ram_1_write_time), .nRead_Write(R_W),
    .Chip_Select(CS), .Start(in_1));
  D_Flip_Flop d_ff_2 (.clk(CLK), .D(d_ff_1_q), .Qn(LCLR), .reset(Reset_out));  // open: Q, preset, en
  or or_1 (RST, LCLR, LoadRAM);
  Clock clock_1 (.out(CLK));
  Multiplexer #(.width(32), .enable("false")) multiplexer_1 (.in0(I0), .in1(LData), .out(RI0), .sel(LoadRAM));
  Multiplexer #(.width(32), .enable("false")) multiplexer_2 (.in0(I1), .in1(LData), .out(RI1), .sel(LoadRAM));
  Multiplexer #(.width(32), .enable("false")) multiplexer_3 (.in0(I2), .in1(LData), .out(RI2), .sel(LoadRAM));
  Multiplexer #(.width(32), .enable("false")) multiplexer_4 (.in0(I3), .in1(LData), .out(RI3), .sel(LoadRAM));
  and and_1 (LoadRAM, ~DESHABILITAR_DISPATCHER, LoadRAMOn);  // AND_Gate
  Multiplexer #(.width(16), .enable("false")) multiplexer_5 (.in0(Addr), .in1(LAddr), .out(RAddr), .sel(LoadRAM));
  Multiplexer #(.width(4), .enable("false")) multiplexer_6 (.in0(Mask), .in1(LMask), .out(RMask), .sel(LoadRAM));
  Multiplexer #(.enable("false")) multiplexer_7 (.in0(CS), .in1(LW), .out(RCS), .sel(LoadRAM));
  Multiplexer #(.enable("false")) multiplexer_8 (.in0(R_W), .in1(LW), .out(R_R_W), .sel(LoadRAM));

  // Notes on the sheet:
  //   NO MODIFICAR
  //   Keyboard
endmodule

module RAM (
  input  [15:0] Address,
  input  [31:0] Data_In_0,
  input  [31:0] Data_In_1,
  input  [31:0] Data_In_2,
  input  [31:0] Data_In_3,
  input  [3:0] Mask,
  input  nRead_Write,
  input  Chip_Select,
  input  Reset,
  output [31:0] Data_Out_0,
  output [31:0] Data_Out_1,
  output [31:0] Data_Out_2,
  output [31:0] Data_Out_3,
  output [3:0] Read_Time,
  output [3:0] Write_Time
);

  wire and_2_out, and_3_out, and_4_out, and_5_out, and_6_out, and_7_out, and_8_out, and_9_out, Changed, CLK,
       comparator_2_eq, comparator_3_eq, comparator_4_eq, comparator_5_eq, comparator_6_eq, Count,
       demultiplexer_3_out0, Idle, Idle_q, Load, Load0, Load1, nand_1_out, or_1_out, or_2_out, or_3_out,
       or_4_out, or_5_out, or_6_out, or_7_out, or_8_out, or_9_out, or_10_out, Proc_q, Update_Mem, Zero_Time;
  wire [3:0] counter_1_q, multiplexer_1_out, subtractor_1_out;
  wire [31:0] register_1_q, register_2_q, register_3_q, register_4_q, register_5_q;

  // Probe on 4'b0011
  // Probe on 4'b0010
  Multiplexer #(.width(4), .enable("false")) multiplexer_1 (
    .in0(4'b0011), .in1(4'b0010), .out(multiplexer_1_out), .sel(nRead_Write));
  or or_1 (or_1_out, Idle, Update_Mem);
  or or_2 (or_2_out, ~Chip_Select, Reset);  // OR_Gate
  Subtractor #(.width(4)) subtractor_1 (.a(multiplexer_1_out), .b(4'b0010), .out(subtractor_1_out));  // open: bin, bout
  D_Flip_Flop u_Idle (.clk(CLK), .D(or_1_out), .Q(Idle_q), .preset(or_2_out));  // open: Qn, en, reset
  Demultiplexer #(.enable("false")) demultiplexer_1 (.out0(Idle), .out1(Load0), .in(Idle_q), .sel(Changed));
  // Probe on counter_1_q
  Counter #(.width(4), .max('hf)) counter_1 (
    .load(Load), .D(subtractor_1_out), .count(Count), .Q(counter_1_q), .clk(CLK), .clr(or_3_out));  // open: carry
  or or_3 (or_3_out, ~Chip_Select, Reset);  // OR_Gate
  Comparator #(.width(4), .mode("unsigned")) comparator_1 (
    .a(4'b0000), .b(counter_1_q), .eq(Zero_Time));  // open: gt, lt
  or or_4 (or_4_out, Count, Load0, Load1);
  Register #(.width(32)) register_1 (.D(Data_In_0), .en(Chip_Select), .Q(register_1_q), .clk(CLK), .clr(or_5_out));
  or or_5 (or_5_out, ~Chip_Select, Reset);  // OR_Gate
  Register #(.width(32)) register_2 (.D(Data_In_1), .en(Chip_Select), .Q(register_2_q), .clk(CLK), .clr(or_6_out));
  or or_6 (or_6_out, ~Chip_Select, Reset);  // OR_Gate
  Register #(.width(32)) register_3 (.D(Data_In_2), .en(Chip_Select), .Q(register_3_q), .clk(CLK), .clr(or_7_out));
  or or_7 (or_7_out, ~Chip_Select, Reset);  // OR_Gate
  Register #(.width(32)) register_4 (.D(Data_In_3), .en(Chip_Select), .Q(register_4_q), .clk(CLK), .clr(or_8_out));
  or or_8 (or_8_out, ~Chip_Select, Reset);  // OR_Gate
  Register #(.width(32)) register_5 (
    .D({{11{1'b1}}, nRead_Write, Mask, Address}), .en(Chip_Select), .Q(register_5_q), .clk(CLK),
    .clr(or_9_out));
  or or_9 (or_9_out, ~Chip_Select, Reset);  // OR_Gate
  D_Flip_Flop Proc (.clk(CLK), .D(or_4_out), .Q(Proc_q), .reset(or_10_out));  // open: Qn, preset, en
  or or_10 (or_10_out, ~Chip_Select, Reset);  // OR_Gate
  Demultiplexer #(.enable("false")) demultiplexer_2 (
    .out0(Count), .out1(Update_Mem), .in(demultiplexer_3_out0), .sel(Zero_Time));
  Demultiplexer #(.enable("false")) demultiplexer_3 (
    .out0(demultiplexer_3_out0), .out1(Load1), .in(Proc_q), .sel(Changed));
  Clock clock_1 (.out(CLK));
  Comparator #(.width(32)) comparator_2 (.a(register_1_q), .b(Data_In_0), .eq(comparator_2_eq));  // open: gt, lt
  Comparator #(.width(32)) comparator_3 (.a(register_2_q), .b(Data_In_1), .eq(comparator_3_eq));  // open: gt, lt
  Comparator #(.width(32)) comparator_4 (.a(register_3_q), .b(Data_In_2), .eq(comparator_4_eq));  // open: gt, lt
  Comparator #(.width(32)) comparator_5 (.a(register_4_q), .b(Data_In_3), .eq(comparator_5_eq));  // open: gt, lt
  Comparator #(.width(32)) comparator_6 (
    .a(register_5_q), .b({{11{1'b1}}, nRead_Write, Mask, Address}), .eq(comparator_6_eq));  // open: gt, lt
  nand nand_1 (nand_1_out, comparator_6_eq, comparator_2_eq, comparator_3_eq, comparator_4_eq, comparator_5_eq);
  and and_1 (Changed, nand_1_out, Chip_Select);
  or or_11 (Load, Count, Load1, Load0);
  and and_2 (and_2_out, Mask[0], Update_Mem, nRead_Write);
  and and_3 (and_3_out, Mask[1], Update_Mem, nRead_Write);
  and and_4 (and_4_out, Mask[2], Update_Mem, nRead_Write);
  and and_5 (and_5_out, Mask[3], Update_Mem, nRead_Write);
  RAM_part #(.addrWidth(16), .dataWidth(32), .bus("separate")) ram_1 (
    .addr(Address), .din(Data_In_0), .data(Data_Out_0), .str(and_2_out), .sel(Chip_Select), .clk(CLK),
    .ld(and_6_out), .clr(Reset));
  and and_6 (and_6_out, ~nRead_Write, Idle);  // AND_Gate
  RAM_part #(.addrWidth(16), .dataWidth(32), .bus("separate")) ram_2 (
    .addr(Address), .din(Data_In_1), .data(Data_Out_1), .str(and_3_out), .sel(Chip_Select), .clk(CLK),
    .ld(and_7_out), .clr(Reset));
  and and_7 (and_7_out, ~nRead_Write, Idle);  // AND_Gate
  RAM_part #(.addrWidth(16), .dataWidth(32), .bus("separate")) ram_3 (
    .addr(Address), .din(Data_In_2), .data(Data_Out_2), .str(and_4_out), .sel(Chip_Select), .clk(CLK),
    .ld(and_8_out), .clr(Reset));
  and and_8 (and_8_out, ~nRead_Write, Idle);  // AND_Gate
  RAM_part #(.addrWidth(16), .dataWidth(32), .bus("separate")) ram_4 (
    .addr(Address), .din(Data_In_3), .data(Data_Out_3), .str(and_5_out), .sel(Chip_Select), .clk(CLK),
    .ld(and_9_out), .clr(Reset));
  and and_9 (and_9_out, ~nRead_Write, Idle);  // AND_Gate

  assign Read_Time = 4'b0011;
  assign Write_Time = 4'b0010;

  // Other names for the same wires on the sheet: M0 = Mask[0]; M1 = Mask[1]; M2 = Mask[2]; M3 = Mask[3];
  //   RW = nRead_Write; CLR = Reset; CS = Chip_Select; Load2 = Count

  // Notes on the sheet:
  //   NO MODIFICAR
  //   excepto quizás los valores RT y WT
  //   BANK0
  //   BANK1
  //   BANK2
  //   BANK3
endmodule

module S_MIPS (
  input  Kbd_Available,
  input  [6:0] Kbd_ASCII_Data,
  input  [31:0] RAM_Out_0,
  input  [31:0] RAM_Out_1,
  input  Reset,
  input  [31:0] RAM_Out_2,
  input  Clock,
  input  [31:0] RAM_Out_3,
  input  Start,
  input  [3:0] Read_Time,
  input  [3:0] Write_Time,
  output Kbd_Enable,
  output [15:0] Address,
  output Kbd_Clear,
  output TTY_Enable,
  output [6:0] TTY_ASCII_Data,
  output Stop,
  output [31:0] RAM_In_0,
  output [31:0] RAM_In_1,
  output [31:0] RAM_In_2,
  output [31:0] RAM_In_3,
  output [3:0] Mask,
  output nRead_Write,
  output Chip_Select
);

  wire Enable_Inst, Finish_RAM, HALT, PC_Address, PC_Enable, READ_RAM, WRITE_RAM;
  wire [31:0] Instruction, RAM_Address, Value_Write_RAM;

  Control_Unit control_unit_1 (
    .Read_Time(Read_Time), .Read_RAM(READ_RAM), .Write_Time(Write_Time), .Write_RAM(WRITE_RAM),
    .CS(Chip_Select), .END(Stop), .Start(Start), .Clock(Clock), .Reset(Reset), .Is__Halt(HALT),
    .PC_Enable(PC_Enable), .PC_Address(PC_Address), .Finish_RAM(Finish_RAM), .R_W_RAM(nRead_Write),
    .Enable_Inst(Enable_Inst));
  Read_RAM read_ram_1 (
    .Bank_0(RAM_Out_0), .Bank_1(RAM_Out_1), .Bank_2(RAM_Out_2), .Bank_3(RAM_Out_3),
    .Instruction(Instruction), .Address_RAM(RAM_Address));
  Write_RAM write_ram_1 (
    .Address_RAM(RAM_Address), .Value_Input(Value_Write_RAM), .Bank_0(RAM_In_0), .Bank_1(RAM_In_1),
    .Bank_2(RAM_In_2), .Bank_3(RAM_In_3), .Mask(Mask), .RAM_OUT(Address));
  DATA_PATH_2 data_path_1 (
    .Clock(Clock), .Reset(Reset), .KBD_AVAIL(Kbd_Available), .Keyboard(Kbd_ASCII_Data),
    .PC_address(PC_Address), .Intruction(Instruction), .Address_Inst_RAM(RAM_Address),
    .Value_Write_in_RAM(Value_Write_RAM), .HALT(HALT), .Read_from_RAM(READ_RAM), .KBD(Kbd_Enable),
    .Write_To_RAM(WRITE_RAM), .TTY(TTY_Enable), .TTY_DATA(TTY_ASCII_Data), .PC_Enable(PC_Enable),
    .Work_RAM_finish(Finish_RAM), .Enable_Inst(Enable_Inst));

  assign Kbd_Clear = Reset;

  // Other names for the same wires on the sheet: CLK = Clock; CLR = Reset; CS = Chip_Select;
  //   KBD_AVAIL = Kbd_Available; KBD_DATA[6:0] = Kbd_ASCII_Data; R_W = nRead_Write; RAM_INPUT_0[31:0] = RAM_In_0;
  //   RAM_INPUT_1[31:0] = RAM_In_1; RAM_INPUT_2[31:0] = RAM_In_2; RAM_INPUT_3[31:0] = RAM_In_3; RAM_MASK[3:0] = Mask;
  //   RAM_OUT[15:0] = Address; RAM_OUTPUT_0[31:0] = RAM_Out_0; RAM_OUTPUT_1[31:0] = RAM_Out_1;
  //   RAM_OUTPUT_2[31:0] = RAM_Out_2; RAM_OUTPUT_3[31:0] = RAM_Out_3; TTY_DATA[6:0] = TTY_ASCII_Data

  // Notes on the sheet:
  //   RAM ADDRESS
  //   DATA FROM RAM
  //   DATA TO RAM
  //   DATA WRITE MASK
  //   RAM TIMING
  //   RAM CONTROL
  //   KEYBOARD
  //   TTY
  //   SEQUENCING
endmodule

module RAM_Dispatcher (
  input  [3:0] WriteTime,
  input  Clock,
  input  CLR,
  output [31:0] Data,
  output [15:0] Address,
  output [3:0] Mask,
  output Finished,
  output Write
);

  wire demultiplexer_2_out1, demultiplexer_3_out1, End, IDLE_q, IncAddr, Load, or_1_out, or_2_out, While_q,
       WriteEnd;
  wire [3:0] counter_1_q;
  wire [31:0] CurrentAddress_q;

  Counter #(.width(32), .max('hffffffff)) CurrentAddress (
    .count(IncAddr), .Q({CurrentAddress_q[31:18], Address, CurrentAddress_q[1:0]}), .clk(Clock), .clr(CLR));  // open: load, D, carry
  or or_1 (or_1_out, IncAddr, demultiplexer_3_out1, Finished);
  D_Flip_Flop IDLE (.clk(Clock), .D(or_1_out), .Q(IDLE_q), .preset(CLR));  // open: Qn, en, reset
  Demultiplexer #(.enable("false")) demultiplexer_1 (.out0(Load), .out1(Finished), .in(IDLE_q), .sel(End));
  D_Flip_Flop While (.clk(Clock), .D(or_2_out), .Q(While_q), .reset(CLR));  // open: Qn, preset, en
  or or_2 (or_2_out, Write, Load);
  RAM_part #(.addrWidth(18), .dataWidth(32)) ram_1 (
    .addr({Address, CurrentAddress_q[1:0]}), .data(Data), .clk(Clock));  // open: sel, ld, clr
  Demultiplexer #(.enable("false")) demultiplexer_2 (
    .out0(Write), .out1(demultiplexer_2_out1), .in(While_q), .sel(WriteEnd));
  Decoder #(.select(2)) decoder_1 (
    .out0(Mask[0]), .out1(Mask[1]), .out2(Mask[2]), .out3(Mask[3]), .sel(CurrentAddress_q[1:0]));  // open: en
  Demultiplexer #(.enable("false")) demultiplexer_3 (
    .out0(IncAddr), .out1(demultiplexer_3_out1), .in(demultiplexer_2_out1), .sel(End));
  Counter #(.width(4), .max('hf)) counter_1 (
    .load(Load), .D(WriteTime), .count(Write), .Q(counter_1_q), .clk(Clock));  // open: carry, clr
  Comparator #(.width(32)) comparator_1 (.a(Data), .b({32{1'b1}}), .eq(End));  // open: gt, lt
  Comparator #(.width(4)) comparator_2 (.a(4'b0000), .b(counter_1_q), .eq(WriteEnd));  // open: gt, lt

  // Other names for the same wires on the sheet: CLK = Clock; Count = Write; WT[3:0] = WriteTime
endmodule

// PC
module Program_Counter (
  input  [31:0] Address,
  input  Clock,
  input  Reset,
  input  Load,
  output [31:0] Address_Instruction
);

  Register #(.width(32)) PC (.D(Address), .en(Load), .Q(Address_Instruction), .clk(Clock), .clr(Reset));
endmodule

module Branch_Control (
  input  Jump,
  input  [31:0] PC_Input,
  input  Jr,
  input  [31:0] Rs,
  input  Nop,
  input  Beq,
  input  [15:0] Offset,
  input  [31:0] Rt,
  input  Bne,
  input  Blez,
  input  [25:0] Destiny,
  input  Bgtz,
  input  Bltz,
  output [31:0] PC_Output
);

  wire Beq_Bne, Bltz_Blez_Bgtz, comparator_1_eq, comparator_1_gt, comparator_1_lt, comparator_2_eq,
       comparator_2_gt, comparator_2_lt, or_1_out, or_2_out;
  wire [1:0] or_4_out;
  wire [15:0] offset_4;
  wire [31:0] PC_4, PC_4_4_offset;

  // Probe on Offset
  Adder #(.width(32)) adder_1 (.a(PC_Input), .b(32'h4), .out(PC_4));  // open: cin, cout
  Multiplier #(.width(16)) multiplier_1 (.a(Offset), .b(16'h4), .out(offset_4));  // open: cin, cout
  Adder #(.width(32)) adder_2 (.a(PC_4), .b({{16{1'b0}}, offset_4}), .out(PC_4_4_offset));  // open: cin, cout
  // Probe on PC_Input
  // Probe on Offset
  // Probe on Destiny
  // Probe on {{16{1'b0}}, offset_4}
  assign PC_Output = Jr ? Rs : 32'bz;  // Controlled_Buffer controlled_buffer_1
  Comparator #(.width(32)) comparator_1 (
    .a(Rs), .b(Rt), .gt(comparator_1_gt), .eq(comparator_1_eq), .lt(comparator_1_lt));
  // Probe on Rs
  // Probe on Rt
  or or_1 (or_1_out, comparator_1_gt, comparator_1_lt);
  Multiplexer #(.select(2), .disabled(0), .enable("false")) multiplexer_1 (
    .in0(1'b0), .in1(comparator_1_eq), .in2(or_1_out), .in3(1'b0), .out(Beq_Bne), .sel({Bne, Beq}));
  Comparator #(.width(32)) comparator_2 (
    .a(Rs), .b({32{1'b0}}), .gt(comparator_2_gt), .eq(comparator_2_eq), .lt(comparator_2_lt));
  or or_2 (or_2_out, comparator_2_eq, comparator_2_lt);
  assign PC_Output = Jump ? {PC_Input[31:28], Destiny, 2'b00} : 32'bz;  // Controlled_Buffer controlled_buffer_2
  or or_3 (or_4_out[1], Beq_Bne, Bltz_Blez_Bgtz);
  Multiplexer #(.select(2), .width(32), .disabled(0), .enable("false")) multiplexer_2 (
    .in0(PC_4), .in1(PC_Output), .in2(PC_4_4_offset), .in3({32{1'b0}}), .out(PC_Output), .sel(or_4_out));
  or or_4 (or_4_out[0], Jr, Jump);
  Multiplexer #(.select(3), .disabled(0), .enable("false")) multiplexer_3 (
    .in0(1'b0), .in1(comparator_2_gt), .in2(or_2_out), .in3(1'b0), .in4(comparator_2_lt), .in5(1'b0),
    .in6(1'b0), .in7(1'b0), .out(Bltz_Blez_Bgtz), .sel({Bltz, Blez, Bgtz}));
  // Probe on PC_Output
  // Probe on PC_Output

  // Notes on the sheet:
  //   Inputs
  //   Outputs
endmodule

module Little_Endian____Big_Endian (
  input  [31:0] Data_Input,
  output [31:0] Data_Output
);


  assign Data_Output = {Data_Input[7:0], Data_Input[15:8], Data_Input[23:16], Data_Input[31:24]};
endmodule

module DATA_PATH_2 (
  input  [31:0] Intruction,
  input  [6:0] Keyboard,
  input  Clock,
  input  Reset,
  input  KBD_AVAIL,
  input  PC_address,
  input  PC_Enable,
  input  Work_RAM_finish,
  input  Enable_Inst,
  output [31:0] Address_Inst_RAM,
  output [31:0] Value_Write_in_RAM,
  output HALT,
  output Read_from_RAM,
  output KBD,
  output Write_To_RAM,
  output TTY,
  output [6:0] TTY_DATA
);

  wire ADD, ADDI, AND, and_1_out, and_2_out, ANDI, BEQ, BGTZ, BLEZ, BLTZ, BNE, DIV, DIVU, E_HL, J, JR, LW,
       MFHI, MFLO, MULT, MULU, Neg, NOP, NOR, OR, or_2_out, or_3_out, or_4_out, or_5_out, or_6_out, or_7_out,
       or_8_out, or_15_out, ORI, POP, PUSH, R_W, RND, SLT, SLTI, SLTIU, SLTU, SUB, SW, TTY_t, Type_I, XOR,
       XORI, Zero;
  wire [2:0] Select_RF;
  wire [3:0] ALU_Selector;
  wire [4:0] multiplexer_3_out, RD, RS, RT;
  wire [15:0] CONST;
  wire [25:0] JUMP;
  wire [31:0] ALU_Output, bit_extender_1_out, bit_extender_2_out, High_ALU, High_RF, Input_RF, KBD_or_Rnd,
       Low_RF, multiplexer_4_out, multiplexer_5_out, Next_PC, PC_Value, register_1_q, SP_Value, Value_RT;
  wire [31:7] Value_RS;

  or or_1 (E_HL, MULT, MULU, DIV, DIVU);
  or or_2 (or_2_out, ADD, SUB, AND, OR);
  or or_3 (or_3_out, NOR, XOR, SLT, SLTU);
  or or_4 (or_4_out, MFHI, MFLO, ADDI, ANDI);
  or or_5 (or_5_out, SLTI, ORI, XORI, SLTIU);
  or or_6 (or_6_out, RND, KBD, E_HL);
  or or_7 (or_7_out, or_2_out, or_3_out, or_4_out, or_5_out, or_6_out);
  or or_8 (or_8_out, LW, POP);
  and and_1 (and_1_out, PC_Enable, or_7_out);
  and and_2 (and_2_out, or_8_out, Work_RAM_finish);
  Inst_Especiales inst_especiales_1 (
    .Keyboard(Keyboard), .KBD_AVAIL(KBD), .Clock(Clock), .Rnd(RND), .KBD_or_Rnd(KBD_or_Rnd));
  or or_9 (R_W, and_1_out, and_2_out);
  or or_10 (Write_To_RAM, SW, PUSH);
  or or_11 (Select_RF[0], KBD, RND);
  or or_12 (Select_RF[1], LW, MFHI, POP);
  or or_13 (Select_RF[2], MFHI, MFLO);
  and and_3 (TTY, TTY_t, PC_Enable);
  Access___RAM access_ram_1 (
    .PC_Input(PC_Value), .SP_Input(SP_Value), .ALU(ALU_Output), .Push(PUSH), .Pop(POP), .Lw(LW), .Sw(SW),
    .POS_RAM(Address_Inst_RAM), .PC_Address(PC_address));
  or or_14 (Read_from_RAM, LW, POP);
  Multiplexer #(.width(32), .enable("false")) multiplexer_1 (
    .in0({Value_RS, TTY_DATA}), .in1(Value_RT), .out(Value_Write_in_RAM), .sel(SW));
  Multiplexer #(.select(3), .width(32), .enable("false")) multiplexer_2 (
    .in0(ALU_Output), .in1(KBD_or_Rnd), .in2(Intruction), .in3(High_RF), .in4(Low_RF), .out(Input_RF),
    .sel(Select_RF));  // open: in5, in6, in7
  Register #(.width(32)) register_1 (.D(Intruction), .en(Enable_Inst), .Q(register_1_q), .clk(Clock), .clr(Reset));
  Multiplexer #(.width(5), .enable("false")) multiplexer_3 (.in0(RD), .in1(RT), .out(multiplexer_3_out), .sel(Type_I));
  Instruction_Decoder instruction_decoder_1 (
    .INSTRUCTION(register_1_q), .RS(RS), .RT(RT), .RD(RD), .CONST(CONST), .JUMP(JUMP), .TYPE_I(Type_I),
    .ADD(ADD), .SUB(SUB), .OR(OR), .AND(AND), .SW(SW), .BLTZ(BLTZ), .J(J), .BEQ(BEQ), .NOR(NOR), .XOR(XOR),
    .SLT(SLT), .SLTU(SLTU), .BNE(BNE), .BLEZ(BLEZ), .BGTZ(BGTZ), .ADDI(ADDI), .MFHI(MFHI), .MFLO(MFLO),
    .MULT(MULT), .MULU(MULU), .SLTI(SLTI), .SLTIU(SLTIU), .ANDI(ANDI), .ORI(ORI), .DIV(DIV), .DIVU(DIVU),
    .NOP(NOP), .JR(JR), .TTY(TTY_t), .RND(RND), .KBD(KBD), .LW(LW), .XORI(XORI), .POP(POP), .PUSH(PUSH),
    .HALT(HALT));
  Register_File register_file_1 (
    .Data_Input(Input_RF), .High(High_ALU), .CLK(Clock), .Reset(Reset), .R_W(R_W), .R_W_H_L(Work_RAM_finish),
    .S_Load(multiplexer_3_out), .S_Out_1(RS), .S_Out_2(RT), .Mfhi(MFHI), .Mflo(MFLO), .Push(PUSH), .Pop(POP),
    .DATA_Output_1({Value_RS, TTY_DATA}), .DATA_HIGH(High_RF), .DATA_Output_2(Value_RT), .DATA_LOW(Low_RF),
    .SP(SP_Value));
  ALU_Coding alu_coding_1 (
    .Add(ADD), .Slt(SLT), .Sub(SUB), .Addi(ADDI), .Slti(SLTI), .Nor(NOR), .And(AND), .Sltu(SLTU),
    .Andi(ANDI), .Sltiu(SLTIU), .Or(OR), .Mult(MULT), .Ori(ORI), .Mulu(MULU), .Div(DIV), .Xor(XOR),
    .Divu(DIVU), .Xori(XORI), .Selector_Operation(ALU_Selector));
  assign bit_extender_1_out = {{16{CONST[15]}}, CONST};  // Bit_Extender bit_extender_1
  assign bit_extender_2_out = {{16{1'b0}}, CONST};  // Bit_Extender bit_extender_2
  Multiplexer #(.width(32), .enable("false")) multiplexer_4 (
    .in0(bit_extender_1_out), .in1(bit_extender_2_out), .out(multiplexer_4_out), .sel(or_15_out));
  or or_15 (or_15_out, ANDI, ORI, XORI);
  Multiplexer #(.width(32), .enable("false")) multiplexer_5 (
    .in0(Value_RT), .in1(multiplexer_4_out), .out(multiplexer_5_out), .sel(Type_I));
  Program_Counter program_counter_1 (
    .Address(Next_PC), .Load(PC_Enable), .Address_Instruction(PC_Value), .Clock(Clock), .Reset(Reset));
  ALU alu_1 (
    .DATA_1({Value_RS, TTY_DATA}), .DATA_2(multiplexer_5_out), .SELECTOR(ALU_Selector),
    .ALU_Result(ALU_Output), .Zero_Flag(Zero), .HIGH(High_ALU), .Negative(Neg));
  Branch_Control branch_control_1 (
    .Jump(J), .PC_Input(PC_Value), .Jr(JR), .Rs({Value_RS, TTY_DATA}), .Nop(NOP), .Beq(BEQ), .Offset(CONST),
    .Rt(Value_RT), .Bne(BNE), .Blez(BGTZ), .Destiny(JUMP), .Bgtz(BLEZ), .Bltz(BLTZ), .PC_Output(Next_PC));

  // Other names for the same wires on the sheet: CLK = Clock; Instruction[31:0] = Intruction;
  //   Value_RS[6:0] = TTY_DATA

  // Notes on the sheet:
  //   Inputs
  //   Outputs
endmodule

module ALU (
  input  [31:0] DATA_1,
  input  [31:0] DATA_2,
  input  [3:0] SELECTOR,
  output [31:0] ALU_Result,
  output [31:0] HIGH,
  output Zero_Flag,
  output Negative
);

  wire Mini_SLT, Mini_SLTU;
  wire [1:0] Select_H_L;
  wire [31:0] ADD, AND, DIV_High, DIV_Low, DIVU_High, DIVU_Low, Low, MULT_High, MULT_Low, MULU_High,
       MULU_Low, NOR, OR, Result__P, SLT, SLTU, SUB, XOR;

  Adder #(.width(32)) adder_1 (.a(DATA_1), .b(DATA_2), .out(ADD));  // open: cin, cout
  Subtractor #(.width(32)) subtractor_1 (.a(DATA_1), .b(DATA_2), .out(SUB));  // open: bin, bout
  Multiplier #(.width(32)) multiplier_1 (.a(DATA_1), .b(DATA_2), .out(MULU_Low), .cout(MULU_High));  // open: cin
  Divider #(.width(32)) divider_1 (.a(DATA_1), .b(DATA_2), .out(DIVU_Low), .rem(DIVU_High));  // open: upper
  Mult_Sig mult_sig_1 (.DATA_1(DATA_1), .DATA_2(DATA_2), .HIGH(MULT_High), .LOW(MULT_Low));
  Div_Sig div_sig_1 (.DATA_1(DATA_1), .DATA_2(DATA_2), .HIGH(DIV_High), .LOW(DIV_Low));
  or or_1 (Select_H_L[0], SELECTOR[1], SELECTOR[2]);
  or or_2 (Select_H_L[1], SELECTOR[0], SELECTOR[2]);
  // Probe on SUB
  assign NOR = ~(DATA_1 | DATA_2);  // NOR_Gate nor_1, 32 bits wide
  assign AND = DATA_1 & DATA_2;  // AND_Gate and_1, 32 bits wide
  assign OR = DATA_1 | DATA_2;  // OR_Gate or_3, 32 bits wide
  assign XOR = DATA_1 ^ DATA_2;  // XOR_Gate xor_1, 32 bits wide
  Multiplexer #(.width(32), .enable("false")) multiplexer_1 (
    .in0(Result__P), .in1(Low), .out(ALU_Result), .sel(SELECTOR[3]));
  Multiplexer #(.select(2), .width(32), .enable("false")) multiplexer_2 (
    .in0(MULT_High), .in1(DIV_High), .in2(MULU_High), .in3(DIVU_High), .out(HIGH), .sel(Select_H_L));
  Comparator #(.width(32)) comparator_1 (.a(DATA_1), .b(DATA_2), .lt(Mini_SLT));  // open: gt, eq
  assign SLT = {{31{1'b0}}, Mini_SLT};  // Bit_Extender bit_extender_1
  Comparator #(.width(32), .mode("unsigned")) comparator_2 (.a(DATA_1), .b(DATA_2), .lt(Mini_SLTU));  // open: gt, eq
  assign SLTU = {{31{1'b0}}, Mini_SLTU};  // Bit_Extender bit_extender_2
  Comparator #(.width(32)) comparator_3 (.a(ALU_Result), .b({32{1'b0}}), .eq(Zero_Flag), .lt(Negative));  // open: gt
  Multiplexer #(.select(2), .width(32), .enable("false")) multiplexer_3 (
    .in0(MULT_Low), .in1(DIV_Low), .in2(MULU_Low), .in3(DIVU_Low), .out(Low), .sel(Select_H_L));
  Multiplexer #(.select(3), .width(32), .enable("false")) multiplexer_4 (
    .in0(ADD), .in1(SUB), .in2(AND), .in3(OR), .in4(NOR), .in5(XOR), .in6(SLT), .in7(SLTU), .out(Result__P),
    .sel(SELECTOR[2:0]));
  // Probe on SLT

  // Other names for the same wires on the sheet: Result[31:0] = ALU_Result; Select[3:0] = SELECTOR;
  //   Select_Basic[2:0] = SELECTOR[2:0]; Select_Aux = SELECTOR[3]

  // Notes on the sheet:
  //   Inputs
  //   Arithmetic
  //   ALU-Operations
  //   Logic
  //   Outputs
  //   Comparison
endmodule

module ALU_Coding (
  input  Add,
  input  Slt,
  input  Sub,
  input  Addi,
  input  Slti,
  input  Nor,
  input  And,
  input  Sltu,
  input  Andi,
  input  Sltiu,
  input  Or,
  input  Mult,
  input  Ori,
  input  Mulu,
  input  Div,
  input  Xor,
  input  Divu,
  input  Xori,
  output [3:0] Selector_Operation
);

  wire ADD_t, AND_t, DIV_t, MUL, OR_t, SLT_t, SLTU_t, XOR_t;

  or or_1 (ADD_t, Add, Addi);
  or or_2 (AND_t, And, Andi);
  or or_3 (OR_t, Or, Ori);
  or or_4 (XOR_t, Xor, Xori);
  or or_5 (Selector_Operation[3], MUL, DIV_t);
  or or_6 (Selector_Operation[2], Nor, XOR_t, SLT_t, SLTU_t);
  or or_7 (SLT_t, Slt, Slti);
  or or_8 (SLTU_t, Sltu, Sltiu);
  or or_9 (MUL, Mult, Mulu);
  or or_10 (DIV_t, Div, Divu);
  or or_11 (Selector_Operation[1], AND_t, OR_t, SLT_t, SLTU_t);
  or or_12 (Selector_Operation[0], Sub, OR_t, XOR_t, SLTU_t);

  // Other names for the same wires on the sheet: bit_0 = Selector_Operation[0]; bit_1 = Selector_Operation[1];
  //   bit_2 = Selector_Operation[2]; bit_3 = Selector_Operation[3]

  // Notes on the sheet:
  //   Operations-Inputs
  //   Bits-Selector
  //   Selector-Output
endmodule

module Instruction_Decoder (
  input  [31:0] INSTRUCTION,
  output ADD,
  output NOR,
  output MFHI,
  output DIV,
  output TTY,
  output SUB,
  output XOR,
  output MFLO,
  output DIVU,
  output RND,
  output AND,
  output SLT,
  output MULT,
  output NOP,
  output KBD,
  output OR,
  output SLTU,
  output MULU,
  output JR,
  output LW,
  output SW,
  output BNE,
  output SLTI,
  output XORI,
  output BLTZ,
  output BLEZ,
  output SLTIU,
  output POP,
  output J,
  output BGTZ,
  output ANDI,
  output PUSH,
  output BEQ,
  output ADDI,
  output ORI,
  output HALT,
  output [4:0] RS,
  output [4:0] RT,
  output [4:0] RD,
  output TYPE_I,
  output [15:0] CONST,
  output [25:0] JUMP
);

  wire _00, _00_I, _00s, _01, _10, _10_I, _11_I, comparator_3_eq, comparator_4_eq, comparator_5_eq,
       I_Special, OP_R, or_1_out, or_2_out, or_3_out;

  // Probe on INSTRUCTION[5:0]
  // Probe on INSTRUCTION[31:26]
  Comparator #(.width(6)) comparator_1 (.a(INSTRUCTION[31:26]), .b({6{1'b0}}), .eq(OP_R));  // open: gt, lt
  Demultiplexer #(.select(4), .enable("false")) demultiplexer_1 (
    .out3(LW), .out11(SW), .in(_10_I), .sel(INSTRUCTION[29:26]));  // open: out0, out1, out2, out4, out5, out6, out7, out8, out9, out10, out12, out13, out14, out15
  Demultiplexer #(.select(2), .enable("false")) demultiplexer_2 (
    .out0(_00), .out1(_01), .out2(_10), .in(OP_R), .sel(INSTRUCTION[5:4]));  // open: out3
  Demultiplexer #(.select(2), .enable("false")) demultiplexer_3 (
    .out0(_00s), .out3(HALT), .in(I_Special), .sel(INSTRUCTION[5:4]));  // open: out1, out2
  Demultiplexer #(.select(4), .enable("false")) demultiplexer_4 (
    .out0(NOP), .out8(JR), .in(_00), .sel(INSTRUCTION[3:0]));  // open: out1, out2, out3, out4, out5, out6, out7, out9, out10, out11, out12, out13, out14, out15
  Comparator #(.width(6)) comparator_2 (.a(INSTRUCTION[31:26]), .b({6{1'b1}}), .eq(I_Special));  // open: gt, lt
  Demultiplexer #(.select(4), .enable("false")) demultiplexer_5 (
    .out0(ADD), .out2(SUB), .out4(AND), .out5(OR), .out8(NOR), .out9(XOR), .out11(SLT), .out12(SLTU),
    .in(_10), .sel(INSTRUCTION[3:0]));  // open: out1, out3, out6, out7, out10, out13, out14, out15
  Demultiplexer #(.select(4), .enable("false")) demultiplexer_6 (
    .out1(TTY), .out2(RND), .out4(KBD), .in(_00s), .sel(INSTRUCTION[3:0]));  // open: out0, out3, out5, out6, out7, out8, out9, out10, out11, out12, out13, out14, out15
  Comparator #(.width(5)) comparator_3 (
    .a(5'b11000), .b({_11_I, INSTRUCTION[29:26]}), .eq(comparator_3_eq));  // open: gt, lt
  Demultiplexer #(.select(4), .enable("false")) demultiplexer_7 (
    .out1(BLTZ), .out2(J), .out4(BEQ), .out5(BNE), .out6(BLEZ), .out7(BGTZ), .out8(ADDI), .out10(SLTI),
    .out11(SLTIU), .out12(ANDI), .out13(ORI), .out14(XORI), .in(_00_I), .sel(INSTRUCTION[29:26]));  // open: out0, out3, out9, out15
  Comparator #(.width(6)) comparator_4 (.a({6{1'b0}}), .b(INSTRUCTION[5:0]), .eq(comparator_4_eq));  // open: gt, lt
  Comparator #(.width(6)) comparator_5 (.a(INSTRUCTION[5:0]), .b(6'b000001), .eq(comparator_5_eq));  // open: gt, lt
  and and_1 (POP, comparator_3_eq, comparator_4_eq);
  and and_2 (PUSH, comparator_5_eq, comparator_3_eq);
  Demultiplexer #(.select(2), .enable("false")) demultiplexer_8 (
    .out0(_00_I), .out2(_10_I), .out3(_11_I), .in(1'b1), .sel(INSTRUCTION[31:30]));  // open: out1
  Demultiplexer #(.select(4), .enable("false")) demultiplexer_9 (
    .out0(MFHI), .out2(MFLO), .out8(MULT), .out9(MULU), .out10(DIV), .out11(DIVU), .in(_01),
    .sel(INSTRUCTION[3:0]));  // open: out1, out3, out4, out5, out6, out7, out12, out13, out14, out15
  or or_1 (or_1_out, ADDI, ANDI, ORI, XORI);
  or or_2 (or_2_out, SLTI, SLTIU);
  or or_3 (or_3_out, BEQ, BNE, BLEZ, BLTZ, BGTZ);
  or or_4 (or_3_out, LW, SW);
  or or_5 (TYPE_I, or_1_out, or_2_out, or_3_out, or_3_out);

  assign CONST = INSTRUCTION[15:0];
  assign JUMP = INSTRUCTION[25:0];
  assign RD = INSTRUCTION[15:11];
  assign RS = INSTRUCTION[25:21];
  assign RT = INSTRUCTION[20:16];

  // Other names for the same wires on the sheet: Func_Code[5:0] = INSTRUCTION[5:0]; SEL[3:0] = INSTRUCTION[3:0];
  //   Op_Code[5:0] = INSTRUCTION[31:26]; Select2[3:0] = INSTRUCTION[29:26]

  // Notes on the sheet:
  //   Outputs
endmodule

module Register_File (
  input  [31:0] Data_Input,
  input  [31:0] High,
  input  CLK,
  input  Reset,
  input  R_W,
  input  R_W_H_L,
  input  [4:0] S_Load,
  input  [4:0] S_Out_1,
  input  [4:0] S_Out_2,
  input  Mfhi,
  input  Mflo,
  input  Push,
  input  Pop,
  output [31:0] DATA_Output_1,
  output [31:0] DATA_HIGH,
  output [31:0] DATA_Output_2,
  output [31:0] DATA_LOW,
  output [31:0] SP
);

  wire L_1, L_2, L_3, L_4, L_5, L_6, L_7, L_8, L_9, L_10, L_11, L_12, L_13, L_14, L_15, L_16, L_17, L_18,
       L_19, L_20, L_21, L_22, L_23, L_24, L_25, L_26, L_27, L_28, L_29, L_30, L_High, L_Low, L_SP, Load_SP;
  wire [31:0] multiplexer_2_out, S_0, S_1, S_2, S_3, S_4, S_5, S_6, S_7, S_8, S_9, S_10, S_11, S_12, S_13,
       S_14, S_15, S_16, S_17, S_18, S_19, S_20, S_21, S_22, S_23, S_24, S_25, S_26, S_27, S_28, S_29, S_30,
       SP__4, SP__4_t, SP_in;

  Decoder #(.select(5), .disabled(0)) decoder_1 (
    .out1(L_1), .out2(L_2), .out3(L_3), .out4(L_4), .out5(L_5), .out6(L_6), .out7(L_7), .out8(L_8),
    .out9(L_9), .out10(L_10), .out11(L_11), .out12(L_12), .out13(L_13), .out14(L_14), .out15(L_15),
    .out16(L_16), .out17(L_17), .out18(L_18), .out19(L_19), .out20(L_20), .out21(L_21), .out22(L_22),
    .out23(L_23), .out24(L_24), .out25(L_25), .out26(L_26), .out27(L_27), .out28(L_28), .out29(L_29),
    .out30(L_30), .out31(L_SP), .sel(S_Load), .en(R_W));  // open: out0
  // Probe on Data_Input
  // Probe on High
  Register #(.width(32)) R0 (.Q(S_0), .clk(CLK));  // open: D, en, clr
  Register #(.width(32)) R8 (.D(Data_Input), .en(L_8), .Q(S_8), .clk(CLK), .clr(Reset));
  Register #(.width(32)) R16 (.D(Data_Input), .en(L_16), .Q(S_16), .clk(CLK), .clr(Reset));
  Register #(.width(32)) R24 (.D(Data_Input), .en(L_24), .Q(S_24), .clk(CLK), .clr(Reset));
  Register #(.width(32)) R25 (.D(Data_Input), .en(L_25), .Q(S_25), .clk(CLK), .clr(Reset));
  // Probe on S_1
  Register #(.width(32)) R1 (.D(Data_Input), .en(L_1), .Q(S_1), .clk(CLK), .clr(Reset));
  Register #(.width(32)) R9 (.D(Data_Input), .en(L_9), .Q(S_9), .clk(CLK), .clr(Reset));
  Register #(.width(32)) R17 (.D(Data_Input), .en(L_17), .Q(S_17), .clk(CLK), .clr(Reset));
  Register #(.width(32)) R2 (.D(Data_Input), .en(L_2), .Q(S_2), .clk(CLK), .clr(Reset));
  Register #(.width(32)) R10 (.D(Data_Input), .en(L_10), .Q(S_10), .clk(CLK), .clr(Reset));
  Register #(.width(32)) R18 (.D(Data_Input), .en(L_18), .Q(S_18), .clk(CLK), .clr(Reset));
  Register #(.width(32)) R26 (.D(Data_Input), .en(L_26), .Q(S_26), .clk(CLK), .clr(Reset));
  Register #(.width(32)) R3 (.D(Data_Input), .en(L_3), .Q(S_3), .clk(CLK), .clr(Reset));
  Register #(.width(32)) R11 (.D(Data_Input), .en(L_11), .Q(S_11), .clk(CLK), .clr(Reset));
  Register #(.width(32)) R19 (.D(Data_Input), .en(L_19), .Q(S_19), .clk(CLK), .clr(Reset));
  Register #(.width(32)) R27 (.D(Data_Input), .en(L_27), .Q(S_27), .clk(CLK), .clr(Reset));
  Register #(.width(32)) R4 (.D(Data_Input), .en(L_4), .Q(S_4), .clk(CLK), .clr(Reset));
  Register #(.width(32)) R12 (.D(Data_Input), .en(L_12), .Q(S_12), .clk(CLK), .clr(Reset));
  Register #(.width(32)) R20 (.D(Data_Input), .en(L_20), .Q(S_20), .clk(CLK), .clr(Reset));
  Register #(.width(32)) R28 (.D(Data_Input), .en(L_28), .Q(S_28), .clk(CLK), .clr(Reset));
  Register #(.width(32)) R5 (.D(Data_Input), .en(L_5), .Q(S_5), .clk(CLK), .clr(Reset));
  Register #(.width(32)) R13 (.D(Data_Input), .en(L_13), .Q(S_13), .clk(CLK), .clr(Reset));
  Register #(.width(32)) R21 (.D(Data_Input), .en(L_21), .Q(S_21), .clk(CLK), .clr(Reset));
  Register #(.width(32)) R29 (.D(Data_Input), .en(L_29), .Q(S_29), .clk(CLK), .clr(Reset));
  Register #(.width(32)) R6 (.D(Data_Input), .en(L_6), .Q(S_6), .clk(CLK), .clr(Reset));
  Register #(.width(32)) R14 (.D(Data_Input), .en(L_14), .Q(S_14), .clk(CLK), .clr(Reset));
  Register #(.width(32)) R22 (.D(Data_Input), .en(L_22), .Q(S_22), .clk(CLK), .clr(Reset));
  Register #(.width(32)) R30 (.D(Data_Input), .en(L_30), .Q(S_30), .clk(CLK), .clr(Reset));
  Register #(.width(32)) R7 (.D(Data_Input), .en(L_7), .Q(S_7), .clk(CLK), .clr(Reset));
  Register #(.width(32)) R15 (.D(Data_Input), .en(L_15), .Q(S_15), .clk(CLK), .clr(Reset));
  Register #(.width(32)) R23 (.D(Data_Input), .en(L_23), .Q(S_23), .clk(CLK), .clr(Reset));
  Register #(.width(32)) u_SP (.D(SP_in), .en(Load_SP), .Q(SP), .clk(CLK), .clr(Reset));
  Decoder #(.select(2), .disabled(0)) decoder_2 (
    .out1(L_High), .out2(L_Low), .sel({Mflo, Mfhi}), .en(R_W_H_L));  // open: out0, out3
  Multiplexer #(.select(5), .width(32), .enable("false")) multiplexer_1 (
    .in0(S_0), .in1(S_1), .in2(S_2), .in3(S_3), .in4(S_4), .in5(S_5), .in6(S_6), .in7(S_7), .in8(S_8),
    .in9(S_9), .in10(S_10), .in11(S_11), .in12(S_12), .in13(S_13), .in14(S_14), .in15(S_15), .in16(S_16),
    .in17(S_17), .in18(S_18), .in19(S_19), .in20(S_20), .in21(S_21), .in22(S_22), .in23(S_23), .in24(S_24),
    .in25(S_25), .in26(S_26), .in27(S_27), .in28(S_28), .in29(S_29), .in30(S_30), .in31(SP),
    .out(DATA_Output_1), .sel(S_Out_1));
  Adder #(.width(32)) adder_1 (.a(SP), .b(32'h4), .out(SP__4));  // open: cin, cout
  Subtractor #(.width(32)) subtractor_1 (.a(SP), .b(32'h4), .out(SP__4_t));  // open: bin, bout
  // Probe on DATA_Output_1
  Register #(.width(32)) u_HIGH (.D(High), .en(L_High), .Q(DATA_HIGH), .clk(CLK), .clr(Reset));
  Register #(.width(32)) LOW (.D(Data_Input), .en(L_Low), .Q(DATA_LOW), .clk(CLK), .clr(Reset));
  or or_1 (Load_SP, Push, L_SP, Pop);
  Multiplexer #(.width(32), .enable("false")) multiplexer_2 (
    .in0(SP__4), .in1(SP__4_t), .out(multiplexer_2_out), .sel(Push));
  Multiplexer #(.width(32), .enable("false")) multiplexer_3 (
    .in0(Data_Input), .in1(multiplexer_2_out), .out(SP_in), .sel(Pop));
  Multiplexer #(.select(5), .width(32), .enable("false")) multiplexer_4 (
    .in0(S_0), .in1(S_1), .in2(S_2), .in3(S_3), .in4(S_4), .in5(S_5), .in6(S_6), .in7(S_7), .in8(S_8),
    .in9(S_9), .in10(S_10), .in11(S_11), .in12(S_12), .in13(S_13), .in14(S_14), .in15(S_15), .in16(S_16),
    .in17(S_17), .in18(S_18), .in19(S_19), .in20(S_20), .in21(S_21), .in22(S_22), .in23(S_23), .in24(S_24),
    .in25(S_25), .in26(S_26), .in27(S_27), .in28(S_28), .in29(S_29), .in30(S_30), .in31(SP),
    .out(DATA_Output_2), .sel(S_Out_2));
  // Probe on DATA_Output_2

  // Other names for the same wires on the sheet: DATA[31:0] = Data_Input; DATA_Out_1[31:0] = DATA_Output_1;
  //   DATA_Out_2[31:0] = DATA_Output_2; High_Input[31:0] = High; High_Output[31:0] = DATA_HIGH;
  //   Low_Output[31:0] = DATA_LOW; Select_High_Low[1:0] = {Mflo, Mfhi}; Select_Load[4:0] = S_Load;
  //   Select_Out_1[4:0] = S_Out_1; Select_Out_2[4:0] = S_Out_2

  // Notes on the sheet:
  //   Inputs
  //   Registers
  //   Outputs
endmodule

module Inst_Especiales (
  input  [6:0] Keyboard,
  input  KBD_AVAIL,
  input  Clock,
  input  Rnd,
  output [31:0] KBD_or_Rnd
);

  wire [31:0] KBD_register, Result_Rnd;

  Random #(.width(32)) random_1 (.clk(Clock), .next(Rnd), .out(Result_Rnd));  // open: clr
  Multiplexer #(.width(32), .enable("false")) multiplexer_1 (
    .in0({32{1'b1}}), .in1({{25{1'b0}}, Keyboard}), .out(KBD_register), .sel(KBD_AVAIL));
  Multiplexer #(.select(2), .width(32), .enable("false")) multiplexer_2 (
    .in0({32{1'b0}}), .in1(KBD_register), .in2(Result_Rnd), .in3({32{1'b0}}), .out(KBD_or_Rnd),
    .sel({Rnd, KBD_AVAIL}));

  // Other names for the same wires on the sheet: Clk = Clock; Keyboard_extend[6:0] = Keyboard;
  //   Select[1:0] = {Rnd, KBD_AVAIL}

  // Notes on the sheet:
  //   Inputs
  //   Outputs
endmodule

module Mult_Sig (
  input  [31:0] DATA_1,
  input  [31:0] DATA_2,
  output [31:0] HIGH,
  output [31:0] LOW
);

  wire adder_1_cout, Negative_A, Negative_B, Result_Negartive;
  wire [31:0] High_neg, High_neg_Out, Low_neg, Low_neg_Out, multiplexer_1_out, multiplexer_2_out,
       negator_1_data_out, negator_2_data_out, negator_3_out, negator_4_out;

  // Probe on DATA_1
  // Probe on DATA_2
  Negator negator_1 (.DATA_IN(Low_neg), .DATA_OUT(negator_1_data_out));
  Negator negator_2 (.DATA_IN(High_neg), .DATA_OUT(negator_2_data_out));
  Negator_part #(.width(32)) negator_3 (.in(DATA_1), .out(negator_3_out));
  Comparator #(.width(1)) comparator_1 (.a(DATA_1[31]), .b(1'b1), .eq(Negative_A));  // open: gt, lt
  Comparator #(.width(1)) comparator_2 (.a(1'b1), .b(DATA_2[31]), .eq(Negative_B));  // open: gt, lt
  Negator_part #(.width(32)) negator_4 (.in(DATA_2), .out(negator_4_out));
  Adder #(.width(32)) adder_1 (.a(32'h1), .b(negator_1_data_out), .out(Low_neg_Out), .cout(adder_1_cout));  // open: cin
  Multiplexer #(.width(32), .enable("false")) multiplexer_1 (
    .in0(DATA_1), .in1(negator_3_out), .out(multiplexer_1_out), .sel(Negative_A));
  Multiplexer #(.width(32), .enable("false")) multiplexer_2 (
    .in0(DATA_2), .in1(negator_4_out), .out(multiplexer_2_out), .sel(Negative_B));
  Adder #(.width(32)) adder_2 (
    .a({32{1'b0}}), .b(negator_2_data_out), .out(High_neg_Out), .cin(adder_1_cout));  // open: cout
  // Probe on High_neg_Out
  xor xor_1 (Result_Negartive, Negative_A, Negative_B);
  // Probe on multiplexer_1_out
  // Probe on multiplexer_2_out
  // Probe on Low_neg_Out
  Multiplier #(.width(32)) multiplier_1 (
    .a(multiplexer_1_out), .b(multiplexer_2_out), .out(Low_neg), .cout(High_neg));  // open: cin
  // Probe on Low_neg
  // Probe on High_neg
  // Probe on LOW
  Multiplexer #(.width(32), .enable("false")) multiplexer_3 (
    .in0(Low_neg), .in1(Low_neg_Out), .out(LOW), .sel(Result_Negartive));
  Multiplexer #(.width(32), .enable("false")) multiplexer_4 (
    .in0(High_neg), .in1(High_neg_Out), .out(HIGH), .sel(Result_Negartive));
  // Probe on HIGH

  // Notes on the sheet:
  //   Inputs
  //   Outputs
endmodule

module Div_Sig (
  input  [31:0] DATA_1,
  input  [31:0] DATA_2,
  output [31:0] HIGH,
  output [31:0] LOW
);

  wire is_zero, Negative_A, Negative_B, Result_Negartive;
  wire [31:0] cte, minus_neg_division, minus_positive_division, mult_sig_1_low, multiplexer_1_out,
       multiplexer_2_out, neg_division, negator_3_out, negator_4_out, Resto, Result_Div_plus;

  // Probe on DATA_1
  // Probe on DATA_2
  Negator_part #(.width(32)) negator_1 (.in(Result_Div_plus), .out(minus_positive_division));
  Adder #(.width(32)) adder_1 (.a(Result_Div_plus), .b(cte), .out(neg_division));  // open: cin, cout
  Negator_part #(.width(32)) negator_2 (.in(neg_division), .out(minus_neg_division));
  Negator_part #(.width(32)) negator_3 (.in(DATA_1), .out(negator_3_out));
  Comparator #(.width(1)) comparator_1 (.a(DATA_1[31]), .b(1'b1), .eq(Negative_A));  // open: gt, lt
  Comparator #(.width(1)) comparator_2 (.a(1'b1), .b(DATA_2[31]), .eq(Negative_B));  // open: gt, lt
  Negator_part #(.width(32)) negator_4 (.in(DATA_2), .out(negator_4_out));
  Comparator #(.width(32)) comparator_3 (.a(Resto), .b({32{1'b0}}), .eq(is_zero));  // open: gt, lt
  Multiplexer #(.width(32), .enable("false")) multiplexer_1 (
    .in0(DATA_1), .in1(negator_3_out), .out(multiplexer_1_out), .sel(Negative_A));
  Multiplexer #(.width(32), .enable("false")) multiplexer_2 (
    .in0(DATA_2), .in1(negator_4_out), .out(multiplexer_2_out), .sel(Negative_B));
  xor xor_1 (Result_Negartive, Negative_A, Negative_B);
  // Probe on multiplexer_1_out
  // Probe on multiplexer_2_out
  Multiplexer #(.width(32), .enable("false")) multiplexer_3 (.in0(32'h1), .in1({32{1'b0}}), .out(cte), .sel(is_zero));
  Divider #(.width(32)) divider_1 (
    .a(multiplexer_1_out), .b(multiplexer_2_out), .out(Result_Div_plus), .rem(Resto));  // open: upper
  Mult_Sig mult_sig_1 (.DATA_1(DATA_2), .DATA_2(LOW), .LOW(mult_sig_1_low));  // open: HIGH
  Subtractor #(.width(32)) subtractor_1 (.a(DATA_1), .b(mult_sig_1_low), .out(HIGH));  // open: bin, bout
  Multiplexer #(.select(2), .width(32), .enable("false")) multiplexer_4 (
    .in0(Result_Div_plus), .in1(minus_positive_division), .in2(minus_neg_division), .in3(neg_division),
    .out(LOW), .sel({Negative_A, Negative_B}));
  // Probe on HIGH

  // Other names for the same wires on the sheet: selector[1:0] = {Negative_A, Negative_B}

  // Notes on the sheet:
  //   Inputs
  //   Outputs
endmodule

module Control_Unit (
  input  Start,
  input  Clock,
  input  Reset,
  input  Is__Halt,
  input  [3:0] Read_Time,
  input  Read_RAM,
  input  [3:0] Write_Time,
  input  Write_RAM,
  output Finish_RAM,
  output CS,
  output END,
  output PC_Enable,
  output PC_Address,
  output R_W_RAM,
  output Enable_Inst
);

  wire Cap_Inst, Capture, Captured_Inst_q, \cronómetro_2_finish , d_ff_1_q, demultiplexer_1_out0,
       demultiplexer_2_out0, demultiplexer_3_out0, demultiplexer_4_out0, demultiplexer_4_out1,
       demultiplexer_5_out0, Finish, Finish_Proc, IDLE_q, or_1_out, or_2_out, or_4_out, or_6_out, Prox_Inst,
       Reset_Crono_Load, Running, Work_RAM;
  wire [3:0] multiplexer_1_out;

  or or_1 (or_1_out, demultiplexer_1_out0, Start, END);
  or or_2 (or_2_out, Reset_Crono_Load, Prox_Inst);
  D_Flip_Flop IDLE (.clk(Clock), .D(or_1_out), .Q(IDLE_q), .preset(Reset));  // open: Qn, en, reset
  Demultiplexer #(.enable("false")) demultiplexer_1 (
    .out0(demultiplexer_1_out0), .out1(Reset_Crono_Load), .in(IDLE_q), .sel(Start));
  \Cronómetro  \cronómetro_1  (.Count(Read_Time), .CLK(Clock), .Reset(or_2_out), .Finish(Cap_Inst));
  Multiplexer #(.width(4), .disabled(0), .enable("false")) multiplexer_1 (
    .in0(Write_Time), .in1(Read_Time), .out(multiplexer_1_out), .sel(Read_RAM));
  or or_3 (PC_Address, demultiplexer_3_out0, Reset_Crono_Load, Prox_Inst);
  or or_4 (or_4_out, demultiplexer_2_out0, Work_RAM);
  \Cronómetro  \cronómetro_2  (
    .Count(multiplexer_1_out), .CLK(Clock), .Reset(Work_RAM), .Finish(\cronómetro_2_finish ));
  D_Flip_Flop Wait_for_Inst (.clk(Clock), .D(PC_Address), .Q(Capture), .reset(Reset));  // open: Qn, preset, en
  Demultiplexer #(.enable("false")) demultiplexer_2 (
    .out0(demultiplexer_2_out0), .out1(Finish_RAM), .in(d_ff_1_q), .sel(\cronómetro_2_finish ));
  D_Flip_Flop d_ff_1 (.clk(Clock), .D(or_4_out), .Q(d_ff_1_q), .reset(Reset));  // open: Qn, preset, en
  Demultiplexer #(.enable("false")) demultiplexer_3 (
    .out0(demultiplexer_3_out0), .out1(Enable_Inst), .in(Capture), .sel(Cap_Inst));
  or or_5 (Work_RAM, Read_RAM, Write_RAM);
  D_Flip_Flop d_ff_2 (.clk(Clock), .D(Finish_RAM), .Q(Finish), .reset(Reset));  // open: Qn, preset, en
  and and_1 (R_W_RAM, Write_RAM, d_ff_1_q);
  Demultiplexer #(.enable("false")) demultiplexer_4 (
    .out0(demultiplexer_4_out0), .out1(demultiplexer_4_out1), .in(Captured_Inst_q), .sel(Is__Halt));
  D_Flip_Flop Captured_Inst (.clk(Clock), .D(Enable_Inst), .Q(Captured_Inst_q), .reset(Reset));  // open: Qn, preset, en
  or or_6 (or_6_out, demultiplexer_5_out0, demultiplexer_4_out0);
  D_Flip_Flop #(.trigger("falling")) u_END (
    .clk(Clock), .D(PC_Enable), .Q(Finish_Proc), .reset(Reset));  // open: Qn, preset, en
  D_Flip_Flop Execution (.clk(Clock), .D(or_6_out), .Q(Running), .reset(Reset));  // open: Qn, preset, en
  D_Flip_Flop #(.trigger("falling")) END_2 (
    .clk(Clock), .D(demultiplexer_4_out1), .Q(END), .reset(Reset));  // open: Qn, preset, en
  or or_7 (PC_Enable, Running, Finish);
  Demultiplexer #(.enable("false")) demultiplexer_5 (
    .out0(demultiplexer_5_out0), .out1(Prox_Inst), .in(Running), .sel(Finish_Proc));
  LED led_1 (.in(END));
  or or_8 (CS, Work_RAM, Capture);

  // Other names for the same wires on the sheet: Clk = Clock

  // Notes on the sheet:
  //   Inputs
  //   Outputs
endmodule

module \Cronómetro  (
  input  [3:0] Count,
  input  CLK,
  input  Reset,
  output Finish
);

  wire [3:0] counter_1_q;

  Counter #(.width(4), .max('hf), .ongoal("load")) counter_1 (
    .count(1'b1), .Q(counter_1_q), .clk(CLK), .clr(Reset));  // open: load, D, carry
  // Probe on counter_1_q
  Comparator #(.width(4), .mode("unsigned")) comparator_1 (.a(Count), .b(counter_1_q), .eq(Finish));  // open: gt, lt
endmodule

module Read_RAM (
  input  [31:0] Bank_0,
  input  [31:0] Bank_1,
  input  [31:0] Bank_2,
  input  [31:0] Bank_3,
  input  [31:0] Address_RAM,
  output [31:0] Instruction
);

  wire [31:0] multiplexer_1_out;

  Multiplexer #(.select(2), .width(32), .enable("false")) multiplexer_1 (
    .in0(Bank_0), .in1(Bank_1), .in2(Bank_2), .in3(Bank_3), .out(multiplexer_1_out), .sel(Address_RAM[3:2]));
  Little_Endian____Big_Endian little_endian_big_endian_1 (.Data_Input(multiplexer_1_out), .Data_Output(Instruction));

  // Other names for the same wires on the sheet: Mask[1:0] = Address_RAM[3:2]; Input_Bank_0[31:0] = Bank_0;
  //   Input_Bank_1[31:0] = Bank_1; Input_Bank_2[31:0] = Bank_2; Input_Bank_3[31:0] = Bank_3;
  //   Instruction_Out[31:0] = Instruction

  // Notes on the sheet:
  //   Inputs
  //   Outputs
endmodule

module Write_RAM (
  input  [31:0] Address_RAM,
  input  [31:0] Value_Input,
  output [31:0] Bank_0,
  output [31:0] Bank_1,
  output [31:0] Bank_2,
  output [31:0] Bank_3,
  output [3:0] Mask,
  output [15:0] RAM_OUT
);

  wire [31:0] little_endian_big_endian_1_data_output;

  Demultiplexer #(.select(2), .enable("false")) demultiplexer_1 (
    .out0(Mask[0]), .out1(Mask[1]), .out2(Mask[2]), .out3(Mask[3]), .in(1'b1), .sel(Address_RAM[3:2]));
  Little_Endian____Big_Endian little_endian_big_endian_1 (
    .Data_Input(Value_Input), .Data_Output(little_endian_big_endian_1_data_output));
  Demultiplexer #(.select(2), .width(32), .enable("false")) demultiplexer_2 (
    .out0(Bank_0), .out1(Bank_1), .out2(Bank_2), .out3(Bank_3), .in(little_endian_big_endian_1_data_output),
    .sel(Address_RAM[3:2]));

  assign RAM_OUT = Address_RAM[19:4];

  // Other names for the same wires on the sheet: Select_Bank[1:0] = Address_RAM[3:2];
  //   Address[15:0] = Address_RAM[19:4]

  // Notes on the sheet:
  //   Inputs
  //   Outputs
endmodule

module Access___RAM (
  input  [31:0] PC_Input,
  input  [31:0] SP_Input,
  input  [31:0] ALU,
  input  Push,
  input  Pop,
  input  Lw,
  input  Sw,
  input  PC_Address,
  output [31:0] POS_RAM
);

  wire [1:0] Select;
  wire [31:0] multiplexer_1_out, subtractor_1_out;

  Subtractor #(.width(32)) subtractor_1 (.a(SP_Input), .b(32'h4), .out(subtractor_1_out));  // open: bin, bout
  Multiplexer #(.width(32), .enable("false")) multiplexer_1 (
    .in0(SP_Input), .in1(subtractor_1_out), .out(multiplexer_1_out), .sel(Push));
  or or_1 (Select[1], Push, PC_Address, Pop);
  or or_2 (Select[0], Lw, PC_Address, Sw);
  Multiplexer #(.select(2), .width(32), .enable("false")) multiplexer_2 (
    .in0(PC_Input), .in1(ALU), .in2(multiplexer_1_out), .in3(PC_Input), .out(POS_RAM), .sel(Select));

  // Other names for the same wires on the sheet: PC[31:0] = PC_Input; SP[31:0] = SP_Input

  // Notes on the sheet:
  //   Inputs
  //   Outputs
endmodule

module Negator (
  input  [31:0] DATA_IN,
  output [31:0] DATA_OUT
);

  not not_1 (DATA_OUT[0], DATA_IN[0]);
  not not_2 (DATA_OUT[1], DATA_IN[1]);
  not not_3 (DATA_OUT[2], DATA_IN[2]);
  not not_4 (DATA_OUT[3], DATA_IN[3]);
  not not_5 (DATA_OUT[4], DATA_IN[4]);
  not not_6 (DATA_OUT[5], DATA_IN[5]);
  not not_7 (DATA_OUT[6], DATA_IN[6]);
  not not_8 (DATA_OUT[7], DATA_IN[7]);
  not not_9 (DATA_OUT[8], DATA_IN[8]);
  not not_10 (DATA_OUT[9], DATA_IN[9]);
  not not_11 (DATA_OUT[10], DATA_IN[10]);
  not not_12 (DATA_OUT[11], DATA_IN[11]);
  not not_13 (DATA_OUT[12], DATA_IN[12]);
  not not_14 (DATA_OUT[13], DATA_IN[13]);
  not not_15 (DATA_OUT[14], DATA_IN[14]);
  not not_16 (DATA_OUT[15], DATA_IN[15]);
  not not_17 (DATA_OUT[16], DATA_IN[16]);
  not not_18 (DATA_OUT[17], DATA_IN[17]);
  not not_19 (DATA_OUT[18], DATA_IN[18]);
  not not_20 (DATA_OUT[19], DATA_IN[19]);
  not not_21 (DATA_OUT[20], DATA_IN[20]);
  not not_22 (DATA_OUT[21], DATA_IN[21]);
  not not_23 (DATA_OUT[22], DATA_IN[22]);
  not not_24 (DATA_OUT[23], DATA_IN[23]);
  not not_25 (DATA_OUT[24], DATA_IN[24]);
  not not_26 (DATA_OUT[25], DATA_IN[25]);
  not not_27 (DATA_OUT[26], DATA_IN[26]);
  not not_28 (DATA_OUT[27], DATA_IN[27]);
  not not_29 (DATA_OUT[28], DATA_IN[28]);
  not not_30 (DATA_OUT[29], DATA_IN[29]);
  not not_31 (DATA_OUT[30], DATA_IN[30]);
  not not_32 (DATA_OUT[31], DATA_IN[31]);
endmodule
